// Logisim project RAM Module.circ as structural Verilog: 1 circuit, main circuit main
module main (
  input  WE,
  input  WE_2,
  input  Adress,
  input  [7:0] DataIn,
  input  [3:0] Adress_2,
  input  [7:0] DataIn_2,
  output [7:0] DataOut,
  output [7:0] DataOut_2
);

  wire and_1_out, and_2_out, and_3_out, and_4_out, and_5_out, and_6_out, and_7_out, and_8_out, and_9_out,
       and_10_out, and_11_out, and_12_out, and_13_out, and_14_out, and_15_out, and_16_out, and_17_out,
       and_18_out, clock_1_out, clock_2_out, decoder_1_out0, decoder_1_out1, decoder_2_out0, decoder_2_out1,
       decoder_2_out2, decoder_2_out3, decoder_2_out4, decoder_2_out5, decoder_2_out6, decoder_2_out7,
       decoder_2_out8, decoder_2_out9, decoder_2_out10, decoder_2_out11, decoder_2_out12, decoder_2_out13,
       decoder_2_out14, decoder_2_out15;
  wire [7:0] Reg0_2_q, Reg0_q, Reg1_2_q, Reg1_3_q, Reg1_4_q, Reg1_5_q, Reg1_6_q, Reg1_7_q, Reg1_8_q,
       Reg1_9_q, Reg1_10_q, Reg1_11_q, Reg1_12_q, Reg1_13_q, Reg1_14_q, Reg1_15_q, Reg1_16_q, Reg1_q;

  Clock clock_1 (.out(clock_1_out));
  Decoder decoder_1 (.out0(decoder_1_out0), .out1(decoder_1_out1), .en(Adress));  // open: sel
  Register Reg0 (.D(DataIn), .en(and_1_out), .Q(Reg0_q), .clk(clock_1_out));  // open: clr
  Register Reg1 (.D(DataIn), .en(and_2_out), .Q(Reg1_q), .clk(clock_1_out));  // open: clr
  and and_1 (and_1_out, decoder_1_out0, WE_2);
  and and_2 (and_2_out, decoder_1_out1, WE_2);
  Multiplexer #(.width(8)) multiplexer_1 (.in0(Reg0_q), .in1(Reg1_q), .out(DataOut), .sel(Adress));  // open: en
  Clock clock_2 (.out(clock_2_out));
  Decoder #(.select(4)) decoder_2 (
    .out0(decoder_2_out0), .out1(decoder_2_out1), .out2(decoder_2_out2), .out3(decoder_2_out3),
    .out4(decoder_2_out4), .out5(decoder_2_out5), .out6(decoder_2_out6), .out7(decoder_2_out7),
    .out8(decoder_2_out8), .out9(decoder_2_out9), .out10(decoder_2_out10), .out11(decoder_2_out11),
    .out12(decoder_2_out12), .out13(decoder_2_out13), .out14(decoder_2_out14), .out15(decoder_2_out15),
    .sel(Adress_2));  // open: en
  Register Reg0_2 (.D(DataIn_2), .en(and_3_out), .Q(Reg0_2_q), .clk(clock_2_out));  // open: clr
  Register Reg1_2 (.D(DataIn_2), .en(and_4_out), .Q(Reg1_2_q), .clk(clock_2_out));  // open: clr
  Register Reg1_3 (.D(DataIn_2), .en(and_5_out), .Q(Reg1_3_q), .clk(clock_2_out));  // open: clr
  Register Reg1_4 (.D(DataIn_2), .en(and_6_out), .Q(Reg1_4_q), .clk(clock_2_out));  // open: clr
  Register Reg1_5 (.D(DataIn_2), .en(and_8_out), .Q(Reg1_5_q), .clk(clock_2_out));  // open: clr
  Register Reg1_6 (.D(DataIn_2), .en(and_7_out), .Q(Reg1_6_q), .clk(clock_2_out));  // open: clr
  Register Reg1_7 (.D(DataIn_2), .en(and_9_out), .Q(Reg1_7_q), .clk(clock_2_out));  // open: clr
  Register Reg1_8 (.D(DataIn_2), .en(and_10_out), .Q(Reg1_8_q), .clk(clock_2_out));  // open: clr
  Register Reg1_9 (.D(DataIn_2), .en(and_11_out), .Q(Reg1_9_q), .clk(clock_2_out));  // open: clr
  Register Reg1_10 (.D(DataIn_2), .en(and_12_out), .Q(Reg1_10_q), .clk(clock_2_out));  // open: clr
  Register Reg1_11 (.D(DataIn_2), .en(and_13_out), .Q(Reg1_11_q), .clk(clock_2_out));  // open: clr
  Register Reg1_12 (.D(DataIn_2), .en(and_14_out), .Q(Reg1_12_q), .clk(clock_2_out));  // open: clr
  Register Reg1_13 (.D(DataIn_2), .en(and_15_out), .Q(Reg1_13_q), .clk(clock_2_out));  // open: clr
  Register Reg1_14 (.D(DataIn_2), .en(and_16_out), .Q(Reg1_14_q), .clk(clock_2_out));  // open: clr
  Register Reg1_15 (.D(DataIn_2), .en(and_17_out), .Q(Reg1_15_q), .clk(clock_2_out));  // open: clr
  Register Reg1_16 (.D(DataIn_2), .en(and_18_out), .Q(Reg1_16_q), .clk(clock_2_out));  // open: clr
  and and_3 (and_3_out, decoder_2_out0, WE);
  and and_4 (and_4_out, decoder_2_out1, WE);
  and and_5 (and_5_out, decoder_2_out2, WE);
  and and_6 (and_6_out, decoder_2_out3, WE);
  and and_7 (and_7_out, decoder_2_out5, WE);
  and and_8 (and_8_out, decoder_2_out4, WE);
  and and_9 (and_9_out, decoder_2_out6, WE);
  and and_10 (and_10_out, decoder_2_out7, WE);
  and and_11 (and_11_out, decoder_2_out8, WE);
  and and_12 (and_12_out, decoder_2_out9, WE);
  and and_13 (and_13_out, decoder_2_out10, WE);
  and and_14 (and_14_out, decoder_2_out11, WE);
  and and_15 (and_15_out, decoder_2_out12, WE);
  and and_16 (and_16_out, decoder_2_out13, WE);
  and and_17 (and_17_out, decoder_2_out14, WE);
  and and_18 (and_18_out, decoder_2_out15, WE);
  Multiplexer #(.select(4), .width(8)) multiplexer_2 (
    .in0(Reg0_2_q), .in1(Reg1_2_q), .in2(Reg1_3_q), .in3(Reg1_4_q), .in4(Reg1_5_q), .in5(Reg1_6_q),
    .in6(Reg1_7_q), .in7(Reg1_8_q), .in8(Reg1_9_q), .in9(Reg1_10_q), .in10(Reg1_11_q), .in11(Reg1_12_q),
    .in12(Reg1_13_q), .in13(Reg1_14_q), .in14(Reg1_15_q), .in15(Reg1_16_q), .out(DataOut_2), .sel(Adress_2));  // open: en
endmodule
